// Logisim project Universalshiftregister.circ as structural Verilog: 1 circuit, main circuit main
module main (
  input  D,
  input  [3:0] Inp,
  input  [1:0] Set,
  input  R,
  output [3:0] out_5
);

  wire CLK_out, multiplexer_1_out, multiplexer_2_out, multiplexer_3_out, multiplexer_4_out;

  Clock CLK (.out(CLK_out));
  Multiplexer #(.select(2)) multiplexer_1 (
    .in0(D), .in1(out_5[1]), .in2(Inp[0]), .in3(out_5[0]), .out(multiplexer_1_out), .sel(Set));
  D_Flip_Flop d_ff_1 (.D(multiplexer_1_out), .clk(CLK_out), .Q(out_5[0]), .reset(R));  // open: Qn, preset
  D_Flip_Flop d_ff_2 (.D(multiplexer_2_out), .clk(CLK_out), .Q(out_5[1]), .reset(R));  // open: Qn, preset
  Multiplexer #(.select(2)) multiplexer_2 (
    .in0(out_5[0]), .in1(out_5[2]), .in2(Inp[1]), .in3(out_5[1]), .out(multiplexer_2_out), .sel(Set));
  Multiplexer #(.select(2)) multiplexer_3 (
    .in0(out_5[1]), .in1(out_5[3]), .in2(Inp[2]), .in3(out_5[2]), .out(multiplexer_3_out), .sel(Set));
  D_Flip_Flop d_ff_3 (.D(multiplexer_3_out), .clk(CLK_out), .Q(out_5[2]), .reset(R));  // open: Qn, preset
  Multiplexer #(.select(2)) multiplexer_4 (
    .in0(out_5[2]), .in1(D), .in2(Inp[3]), .in3(out_5[3]), .out(multiplexer_4_out), .sel(Set));
  D_Flip_Flop d_ff_4 (.D(multiplexer_4_out), .clk(CLK_out), .Q(out_5[3]), .reset(R));  // open: Qn, preset
  LED led_1 (.in(out_5[3]));
  LED led_2 (.in(out_5[2]));
  LED led_3 (.in(out_5[0]));
  LED led_4 (.in(out_5[1]));
endmodule
